# Fritzing sketch TempHumOLEDMATLAB (saved by Fritzing 0.9.3b)
circuit board: 9cm x 7cm
breadboards: 1

parts:
  OLED_I2C1 = OLED 128x64 I2C Monochrome Display
  Temperature_and_humidity_sensor = Humidity and Temperature Sensor RHT03
  Micro_controller = Arduino Nano (Rev3.0)

nets:
  N1: OLED_I2C1.SDA, Micro_controller.A4
  N2: OLED_I2C1.SCK, Micro_controller.A5
  VDD: OLED_I2C1.VDD, Temperature_and_humidity_sensor.Vcc, Micro_controller.3V3
  GND: OLED_I2C1.GND, Temperature_and_humidity_sensor.GND_2, Micro_controller.GND
  N3: Temperature_and_humidity_sensor.Data-signal, Micro_controller.D2
